# Fritzing sketch MyLittleProject (saved by Fritzing 0.9.3b)

parts:
  A1 = 2 channel relay module [package=THT]
  A2 = 2 channel relay module [package=THT]
  A3 = 2 channel relay module [package=THT]
  A4 = 2 channel relay module [package=THT]
  U1 = NodeMCU V1.0
  J1 = Generic male header - 4 pins [form="♂ (male)" package=THT]
  KY-1 = Keyes Relay [package=THT]

nets:
  N1: A1.pin_13, A4.pin_13
  N2: A1.pin_14, A4.pin_14
  N3: A1.pin_15, U1.D2
  N4: A1.pin_16, U1.D3
  N5: A2.pin_15, U1.D4
  N6: A2.pin_16, U1.D5
  N7: A3.pin_15, U1.D6
  N8: U1.D0, J1.PWM
  N9: U1.D1, J1.Z-C
  N10: U1.3V3, KY-1.power
  N11: U1.D7, KY-1.signal

notes:
  Light 1 (+) OUT
  Light 2 (+) OUT
  Line(+) IN
  Fan OUT
  Sub (+) OUT
  230v AC IN
  5V IN
  Spk 1 (+) OUT
  Spk 1 (-) OUT
  Spk 1 (-) IN R
  Spk 1 (+) IN L
  Spk 1 (+) IN R
  Spk 1 (-) IN L
  Spk 2 (+) IN L
  Spk 2 (+) IN R
  Spk 2 (+) OUT
  Spk 2 (-) OUT

custom parts:
  2 channel relay module: 2 channel Relay Module 5V 12V 24V High and Low Level Trigger Relay Control With Optocoupler Two Way relays DC 5 V 12 V 24 V Volt.
  NodeMCU V1.0: ESP9266 based NodeMCU
  Generic male header - 4 pins: Generic male header
  Keyes Relay: The Keyes 5V relay module is suitable for SCM development, home appliance control. It uses a 5V~12V TIL control signal which can control DC / AC signal.
